# Fritzing sketch Polybuzz (saved by Fritzing 0.9.10b)

parts:
  Composant1 = Arduino Mega 2560 (Rev3)
  LED2 = LED - 5mm [color="Red (633nm)" current=0.030 package="5 mm [THT]"]
  LED3 = LED - 5mm [color="Red (633nm)" current=0.030 package="5 mm [THT]"]
  LED4 = LED - 5mm [color="Red (633nm)" current=0.030 package="5 mm [THT]"]
  R1 = Resistor [tolerance=±5% power=0.25 resistance=220 package=THT]
  R2 = Resistor [tolerance=±5% power=0.25 resistance=220 package=THT]
  R3 = Resistor [tolerance=±5% power=0.25 resistance=220 package=THT]
  LCD1 = LCD screen
  U3 = ENCODER_2LED [package=encoder_led_2]
  J1 = Basic Servo
  S12 = Round Pushbutton
  LED5 = LED - 5mm [color="Red (633nm)" current=0.030 package="5 mm [THT]"]
  LED6 = LED - 5mm [color="Red (633nm)" current=0.030 package="5 mm [THT]"]
  LED7 = LED - 5mm [color="Red (633nm)" current=0.030 package="5 mm [THT]"]
  R4 = Resistor [tolerance=±5% power=0.25 resistance=220 package=THT]
  R5 = Resistor [tolerance=±5% power=0.25 resistance=220 package=THT]
  R6 = Resistor [tolerance=±5% power=0.25 resistance=220 package=THT]
  LED8 = LED - 5mm [color="Red (633nm)" current=0.030 package="5 mm [THT]"]
  LED9 = LED - 5mm [color="Red (633nm)" current=0.030 package="5 mm [THT]"]
  LED10 = LED - 5mm [color="Red (633nm)" current=0.030 package="5 mm [THT]"]
  LED12 = LED - 5mm [color="Red (633nm)" current=0.030 package="5 mm [THT]"]
  R7 = Resistor [tolerance=±5% power=0.25 resistance=220 package=THT]
  R9 = Resistor [tolerance=±5% power=0.25 resistance=220 package=THT]
  R11 = Resistor [tolerance=±5% power=0.25 resistance=220 package=THT]
  R12 = Resistor [tolerance=±5% power=0.25 resistance=220 package=THT]
  S13 = Round Pushbutton
  S14 = Round Pushbutton
  S15 = Round Pushbutton
  S16 = Round Pushbutton
  S17 = Round Pushbutton
  S18 = Round Pushbutton
  S19 = Round Pushbutton
  S20 = Round Pushbutton
  S21 = Round Pushbutton

nets:
  N1: Composant1.D21/SCL, LCD1.VSS
  N2: Composant1.D20/SDA, LCD1.VDD
  N3: Composant1.D13_PWM, J1.pulse
  N4: Composant1.D10_PWM, U3.C
  N5: Composant1.D9_PWM, U3.-
  N6: Composant1.D8_PWM, U3.SW
  5V: Composant1.5V, LED2.anode, LED3.anode, LED4.anode, R2.Pin_0, LCD1.DB0, J1.vcc, LED5.anode, LED6.anode, LED7.anode, LED8.anode, LED9.anode, LED10.anode, LED12.anode
  GND: Composant1.GND, LCD1.DB1, J1.gnd, S12.leg0, S13.leg0, S14.leg0, S15.leg0, S16.leg0, S17.leg0, S18.leg0, S19.leg0, S20.leg0, S21.leg0
  N7: Composant1.D34, R12.Pin_1
  N8: Composant1.D35, S21.leg1
  N9: Composant1.D36, R7.Pin_1
  N10: Composant1.D37, S20.leg1
  N11: Composant1.D38, R9.Pin_1
  N12: Composant1.D39, S19.leg1
  N13: Composant1.D40, R11.Pin_1
  N14: Composant1.D41, S18.leg1
  N15: Composant1.D42, R4.Pin_1
  N16: Composant1.D43, S17.leg1
  N17: Composant1.D44, R5.Pin_1
  N18: Composant1.D45, S16.leg1
  N19: Composant1.D46, R6.Pin_1
  N20: Composant1.D47, S15.leg1
  N21: Composant1.D48, R3.Pin_1
  N22: Composant1.D49, S14.leg1
  N23: Composant1.D50, R2.Pin_1
  N24: Composant1.D51, S13.leg1
  N25: Composant1.D52, R1.Pin_1
  N26: Composant1.D53, S12.leg1
