# Fritzing sketch Polybuzz (saved by Fritzing 0.9.10b)
breadboards: 2

parts:
  Composant1 = Arduino Mega 2560 (Rev3)
  LED2 = LED - 5mm [color="Red (633nm)" current=0.030 package="5 mm [THT]"]
  S2 = Momentary Switch [package=ksa_sealed_tac_switch]
  S3 = Momentary Switch [package=ksa_sealed_tac_switch]
  S4 = Momentary Switch [package=ksa_sealed_tac_switch]
  S5 = Momentary Switch [package=ksa_sealed_tac_switch]
  S6 = Momentary Switch [package=ksa_sealed_tac_switch]
  S7 = Momentary Switch [package=ksa_sealed_tac_switch]
  S8 = Momentary Switch [package=ksa_sealed_tac_switch]
  S9 = Momentary Switch [package=ksa_sealed_tac_switch]
  S10 = Momentary Switch [package=ksa_sealed_tac_switch]
  S11 = Momentary Switch [package=ksa_sealed_tac_switch]
  LED3 = LED - 5mm [color="Red (633nm)" current=0.030 package="5 mm [THT]"]
  LED4 = LED - 5mm [color="Red (633nm)" current=0.030 package="5 mm [THT]"]
  LED5 = LED - 5mm [color="Red (633nm)" current=0.030 package="5 mm [THT]"]
  LED6 = LED - 5mm [color="Red (633nm)" current=0.030 package="5 mm [THT]"]
  LED7 = LED - 5mm [color="Red (633nm)" current=0.030 package="5 mm [THT]"]
  LED8 = LED - 5mm [color="Red (633nm)" current=0.030 package="5 mm [THT]"]
  LED9 = LED - 5mm [color="Red (633nm)" current=0.030 package="5 mm [THT]"]
  LED10 = LED - 5mm [color="Red (633nm)" current=0.030 package="5 mm [THT]"]
  LED11 = LED - 5mm [color="Red (633nm)" current=0.030 package="5 mm [THT]"]
  R1 = Resistor [tolerance=±5% power=0.25 resistance=220 package=THT]
  R2 = Resistor [tolerance=±5% power=0.25 resistance=220 package=THT]
  R3 = Resistor [tolerance=±5% power=0.25 resistance=220 package=THT]
  R4 = Resistor [tolerance=±5% power=0.25 resistance=220 package=THT]
  R5 = Resistor [tolerance=±5% power=0.25 resistance=220 package=THT]
  R6 = Resistor [tolerance=±5% power=0.25 resistance=220 package=THT]
  R7 = Resistor [tolerance=±5% power=0.25 resistance=220 package=THT]
  R8 = Resistor [tolerance=±5% power=0.25 resistance=220 package=THT]
  R9 = Resistor [tolerance=±5% power=0.25 resistance=220 package=THT]
  R10 = Resistor [tolerance=±5% power=0.25 resistance=220 package=THT]
  LCD1 = LCD screen  # not connected
  U2 = BTM182 [package=btm182]  # not connected
  U3 = ENCODER_2LED [package=encoder_led_2]  # not connected

nets:
  N1: Composant1.GND, S2.2, S2.4, S3.2, S3.4, S4.2, S4.4, S5.2, S5.4, S6.2, S6.4, S7.2, S7.4, S8.2, S8.4, S9.2, S9.4, S10.2, S10.4, S11.2, S11.4
  N2: Composant1.5V, Composant1.D35, Composant1.D37, Composant1.D39, Composant1.D41, Composant1.D43, Composant1.D45, Composant1.D47, Composant1.D49, Composant1.D51, Composant1.D53, S2.1, S2.3, S3.1, S3.3, S4.1, S4.3, S5.1, S5.3, S6.1, S6.3, S7.1, S7.3, S8.1, S8.3, S9.1, S9.3, S10.1, S10.3, S11.1, S11.3, R1.Pin_1, R2.Pin_1, R3.Pin_1, R4.Pin_1, R5.Pin_1, R6.Pin_1, R7.Pin_1, R8.Pin_1, R9.Pin_1, R10.Pin_1
  N3: Composant1.D34, LED2.cathode
  N4: Composant1.D36, LED3.cathode
  N5: Composant1.D38, LED4.cathode
  N6: Composant1.D40, LED5.cathode
  N7: Composant1.D42, LED6.cathode
  N8: Composant1.D44, LED7.cathode
  N9: Composant1.D46, LED8.cathode
  N10: Composant1.D48, LED9.cathode
  N11: Composant1.D50, LED10.cathode
  N12: Composant1.D52, LED11.cathode
  N13: LED2.anode, R1.Pin_0
  N14: LED3.anode, R2.Pin_0
  N15: LED4.anode, R3.Pin_0
  N16: LED5.anode, R4.Pin_0
  N17: LED6.anode, R5.Pin_0
  N18: LED7.anode, R6.Pin_0
  N19: LED8.anode, R7.Pin_0
  N20: LED9.anode, R8.Pin_0
  N21: LED10.anode, R9.Pin_0
  N22: LED11.anode, R10.Pin_0
